# Fritzing sketch Arduino_Pong (saved by Fritzing 0.8.7b)
circuit board: 6.88566cm x 5.36311cm
breadboards: 1

parts:
  J1 = female pin header, 4 pins [form="♀ (female)"]
  S1 = Pushbutton [package="[THT]"]
  S2 = Pushbutton [package="[THT]"]
  S3 = Pushbutton [package="[THT]"]
  S4 = Pushbutton [package="[THT]"]
  R1 = Resistor [tolerance=±5% resistance=10k package=THT]
  R2 = Resistor [tolerance=±5% resistance=10k package=THT]
  R4 = Resistor [tolerance=±5% resistance=10k package=THT]
  R5 = Resistor [tolerance=±5% resistance=10k package=THT]
  R6 = Resistor [tolerance=±5% resistance=220 package=THT]
  Spkr_- = female pin header, 1 pin [form="♀ (female)"]
  Spkr_+ = female pin header, 1 pin [form="♀ (female)"]
  Part1 = Arduino Uno (Rev3)

nets:
  N1: J1.pin1, R1.Pin_0, R2.Pin_0, R4.Pin_0, R5.Pin_0, Spkr_-.pin1, Part1.GND
  N2: J1.pin2, S1.Pin_1, S1.Pin_2, S2.Pin_1, S2.Pin_2, S3.Pin_1, S3.Pin_2, S4.Pin_1, S4.Pin_2, Part1.5V
  N3: J1.pin3, Part1.A5/SCL
  N4: J1.pin4, Part1.A4/SDA
  N5: S1.Pin_3, S1.Pin_4, R1.Pin_1, Part1.D5_PWM
  N6: S2.Pin_3, S2.Pin_4, R4.Pin_1, Part1.D3_PWM
  N7: S3.Pin_3, S3.Pin_4, R2.Pin_1, Part1.D9_PWM
  N8: S4.Pin_3, S4.Pin_4, R5.Pin_1, Part1.D2
  N9: R6.Pin_0, Part1.D8
  N10: R6.Pin_1, Spkr_+.pin1
